# Fritzing sketch led-blink-atmega8-usbasp (saved by Fritzing 0.9.2b)
breadboards: 1

parts:
  part = MICROCONTROLLER [part_number=ATMEGA8-16PU package=dil28-3-zif_socket]
  USBasp_male_header = AVR 10-pin ICSP Header [package=avr_icsp]
  R1 = Resistor [tolerance=±5% resistance=470 package="1206 [SMD]"]
  LED1 = smd LED [color="Red (633nm)" package="0603 [SMD]"]

nets:
  N1: part.PC6(_RESET), USBasp_male_header.5
  N2: part.VCC, part.AVCC, USBasp_male_header.2, LED1.cathode
  N3: part.GND, part.AGND, USBasp_male_header.4
  N4: part.PB0(ICP), R1.Pin_0
  N5: part.PB3(MOSI_OC2), USBasp_male_header.1
  N6: part.PB4(MISO), USBasp_male_header.9
  N7: part.PB5(SCK), USBasp_male_header.7
  N8: R1.Pin_1, LED1.anode
